# Fritzing sketch Exypno potisma (saved by Fritzing 0.8.7b)
breadboards: 1

parts:
  LCD1 = LCD screen
  Εξάρτημα1 = Arduino Uno (Rev3)
  U2 = POT [package=pot_mammoth]
  LED1 = smd LED [color="Red (633nm)" package="1206 [SMD]"]
  LED2 = smd LED [color="Green (570nm)" package="1206 [SMD]"]
  KY-1 = Keyes Relay [package=THT]
  VCC1 = Battery block 9V
  R2 = Resistor [tolerance=±5% resistance=220 package=THT]
  YL-1 = YL-38 Humitidy Sensor
  M1 = DC Motor
  R3 = Photocell (LDR) [package=THT]
  R4 = Resistor [tolerance=±5% resistance=1k package=THT]

nets:
  VSS: LCD1.VSS, LCD1.VDD, LCD1.LED+, Εξάρτημα1.3V3, U2.E
  N1: LCD1.V0, Εξάρτημα1.D2
  N2: LCD1.RS, Εξάρτημα1.D3_PWM
  N3: LCD1.R/W, Εξάρτημα1.D4
  N4: LCD1.E, Εξάρτημα1.D5_PWM
  N5: LCD1.DB4, Εξάρτημα1.D6_PWM
  GND: LCD1.DB5, Εξάρτημα1.GND, U2.S, KY-1.power, R2.Pin_0, YL-1.GND, R3.pin_0
  N6: LCD1.DB6, Εξάρτημα1.D7
  N7: LCD1.DB7, U2.A
  N8: Εξάρτημα1.A0, YL-1.ANALOG
  N9: Εξάρτημα1.A1, R3.pin_1, R4.Pin_0
  N10: Εξάρτημα1.D10_PWM/SS, KY-1.ground
  N11: Εξάρτημα1.D11_PWM/MOSI, LED2.anode
  N12: Εξάρτημα1.D12/MISO, LED1.anode
  5V: Εξάρτημα1.5V, KY-1.signal, YL-1.VCC, R4.Pin_1
  N13: LED2.cathode, R2.Pin_1
  N14: KY-1.C, VCC1.-
  N15: KY-1.NO, M1.pin_2

custom parts:
  Keyes Relay: The Keyes 5V relay module is suitable for SCM development, home appliance control. It uses a 5V~12V TIL control signal which can control DC / AC signal.
