# Fritzing sketch AutomaticTent-LightSensor (saved by Fritzing 0.9.3b)
breadboards: 1

parts:
  Motor_Driver = ULN2003A breakout board
  Εξάρτημα1 = Arduino Uno (Rev3)
  Stepper_Motor = 28BYJ-48 Stepper Motor
  5V = Power plug
  R1 = Photocell (LDR) [package=THT]
  R2 = Resistor [tolerance=±5% resistance=1k package=THT]

nets:
  N1: Motor_Driver.In_1, Εξάρτημα1.D3_PWM
  N2: Motor_Driver.In_2, Εξάρτημα1.D5_PWM
  N3: Motor_Driver.In_3, Εξάρτημα1.D4
  N4: Motor_Driver.In_4, Εξάρτημα1.D6_PWM
  GND: Motor_Driver.0V, Εξάρτημα1.GND, 5V.GND, R2.Pin_1
  +5V: Motor_Driver.+5V, 5V.VCC
  N5: Motor_Driver.RED_wire, Stepper_Motor.RED
  N6: Motor_Driver.ORANGE_wire, Stepper_Motor.ORANGE
  N7: Motor_Driver.YELLOW_wire, Stepper_Motor.YELLOW
  N8: Motor_Driver.PINK_wire, Stepper_Motor.PINK
  N9: Motor_Driver.BLUE_wire, Stepper_Motor.BLUE
  N10: Εξάρτημα1.A0, R1.pin_1, R2.Pin_0
  N11: Εξάρτημα1.5V, R1.pin_0

notes:
  Εξωτερική τροφοδοσία 5V
  Συνδεσμολογία:
  IN1 -> pin3
  IN2 -> pin5
  IN3 -> pin4
  IN4 -> pin6

custom parts:
  ULN2003A breakout board: ULN2003A 7-way Darlington Transistor Driver on breakoutboard
