# Fritzing sketch SOLAR SYSTEM (saved by Fritzing 0.9.3b)
breadboards: 1

parts:
  Εξάρτημα1 = Arduino Uno (Rev3)
  J1 = Basic Servo
  R1 = Resistor [tolerance=±5% resistance=220 package=THT]
  R2 = Photocell (LDR) [part_number=LDR1 package=THT]
  R3 = Resistor [tolerance=±5% resistance=220 package=THT]
  R4 = Photocell (LDR) [package=THT]

nets:
  N1: Εξάρτημα1.A0, R3.Pin_1, R4.pin_0
  N2: Εξάρτημα1.A1, R1.Pin_1, R2.pin_0
  N3: Εξάρτημα1.D9_PWM, J1.pulse
  5V: Εξάρτημα1.5V, J1.vcc, R2.pin_1, R4.pin_1
  GND: Εξάρτημα1.GND, J1.gnd, R1.Pin_0, R3.Pin_0
