# Fritzing sketch SOLAR-DISTANCE-LED (saved by Fritzing 0.9.3b)
breadboards: 1

parts:
  Εξάρτημα1 = Arduino Uno (Rev3)
  J1 = Basic Servo
  R1 = Resistor [tolerance=±5% resistance=220 package=THT]
  R2 = Photocell (LDR) [part_number=LDR1 package=THT]
  R3 = Resistor [tolerance=±5% resistance=220 package=THT]
  R4 = Photocell (LDR) [package=THT]
  R5 = Resistor [tolerance=±5% resistance=220 package=THT]
  LED1 = LED - 5mm [color="Red (633nm)" package="5 mm [THT]"]
  hc-sr1 = hc-sr04

nets:
  N1: Εξάρτημα1.A0, R3.Pin_1, R4.pin_0
  N2: Εξάρτημα1.A1, R1.Pin_1, R2.pin_0
  N3: Εξάρτημα1.D9_PWM, J1.pulse
  N4: Εξάρτημα1.D11_PWM/MOSI, hc-sr1.Echo
  N5: Εξάρτημα1.D12/MISO, hc-sr1.Trig
  N6: Εξάρτημα1.D13/SCK, LED1.anode
  VCC: Εξάρτημα1.5V, J1.vcc, R2.pin_1, R4.pin_1, hc-sr1.VCC
  GND: Εξάρτημα1.GND, J1.gnd, R1.Pin_0, R3.Pin_0, R5.Pin_0, hc-sr1.GND
  N7: R5.Pin_1, LED1.cathode
