# Fritzing sketch Metal-1 (saved by Fritzing 0.9.3b)
breadboards: 1

parts:
  Εξάρτημα1 = Arduino Uno (Rev3)
  R1 = Resistor [tolerance=±5% resistance=10k package=THT]
  S3 = H-Bridge with L298N
  M1 = DC Motor
  VCC1 = Battery block 9V
  S4 = Pushbutton [package="[THT]"]
  S5 = Pushbutton [package="[THT]"]
  R2 = Resistor [tolerance=±5% resistance=10k package=THT]

nets:
  N1: Εξάρτημα1.D8, S3.IN2
  N2: Εξάρτημα1.D9_PWM, S3.IN1
  N3: Εξάρτημα1.D10_PWM/SS, S3.ENA
  GND: Εξάρτημα1.GND, R1.Pin_0, S3.GND, VCC1.-, R2.Pin_0
  N4: Εξάρτημα1.D2, R1.Pin_1, S4.Pin_1, S4.Pin_2
  N5: Εξάρτημα1.D3_PWM, S5.Pin_1, S5.Pin_2, R2.Pin_1
  N6: Εξάρτημα1.5V, S4.Pin_3, S4.Pin_4, S5.Pin_3, S5.Pin_4
  N7: S3.12V, VCC1.+
  N8: S3.M1-01, M1.pin_2
  N9: S3.M1-02, M1.pin_1

custom parts:
  H-Bridge with L298N: h-bridge
