# Fritzing sketch Metal-2 (saved by Fritzing 0.9.3b)
breadboards: 1

parts:
  Εξάρτημα1 = Arduino Uno (Rev3)
  R1 = Resistor [tolerance=±5% resistance=10k package=THT]
  S3 = H-Bridge with L298N
  M1 = DC Motor
  VCC1 = Battery block 9V
  S4 = Pushbutton [package="[THT]"]
  S5 = Pushbutton [package="[THT]"]
  R2 = Resistor [tolerance=±5% resistance=10k package=THT]
  BREAKOUT1 = ULN2003A breakout board
  MOTOR1 = 28BYJ-48 Stepper Motor

nets:
  N1: Εξάρτημα1.D8, S3.IN2
  N2: Εξάρτημα1.D9_PWM, S3.IN1
  N3: Εξάρτημα1.D10_PWM/SS, S3.ENA
  GND: Εξάρτημα1.GND, R1.Pin_0, S3.GND, VCC1.-, R2.Pin_0
  N4: Εξάρτημα1.D2, R1.Pin_1, S4.Pin_1, S4.Pin_2
  N5: Εξάρτημα1.D3_PWM, S5.Pin_1, S5.Pin_2, R2.Pin_1
  N6: Εξάρτημα1.D4, BREAKOUT1.In_1
  N7: Εξάρτημα1.D5_PWM, BREAKOUT1.In_2
  N8: Εξάρτημα1.D6_PWM, BREAKOUT1.In_3
  N9: Εξάρτημα1.D7, BREAKOUT1.In_4
  N10: Εξάρτημα1.5V, S4.Pin_3, S4.Pin_4, S5.Pin_3, S5.Pin_4
  N11: S3.12V, VCC1.+
  N12: S3.M1-01, M1.pin_2
  N13: S3.M1-02, M1.pin_1
  N14: BREAKOUT1.RED_wire, MOTOR1.RED
  N15: BREAKOUT1.ORANGE_wire, MOTOR1.ORANGE
  N16: BREAKOUT1.YELLOW_wire, MOTOR1.YELLOW
  N17: BREAKOUT1.PINK_wire, MOTOR1.PINK
  N18: BREAKOUT1.BLUE_wire, MOTOR1.BLUE

custom parts:
  H-Bridge with L298N: h-bridge
  ULN2003A breakout board: ULN2003A 7-way Darlington Transistor Driver on breakoutboard
