# Fritzing sketch Metal-4 (saved by Fritzing 0.9.3b)
breadboards: 1

parts:
  Εξάρτημα1 = Arduino Uno (Rev3)
  R1 = Resistor [tolerance=±5% resistance=10k package=THT]
  S3 = H-Bridge with L298N
  M1 = DC Motor
  VCC1 = Battery block 9V
  S4 = Pushbutton [package="[THT]"]
  BREAKOUT1 = ULN2003A breakout board
  MOTOR1 = 28BYJ-48 Stepper Motor
  ΕΠΑΓΩΓΙΚΟΣ_ΑΙΣΘΗΤΗΡΑΣ = mystery part, 3 pins [chip_label=SENSOR]
  R3 = Resistor [tolerance=±5% resistance=10k package=THT]
  12V_Τροφοδοτικό = Power plug
  MS2 = BGL-My Micro Switch [package=THT]
  MS3 = BGL-My Micro Switch [package=THT]
  R2 = Resistor [tolerance=±5% resistance=10k package=THT]
  S6 = Pushbutton [package="[THT]"]

nets:
  N1: Εξάρτημα1.D8, S3.IN2
  N2: Εξάρτημα1.D9_PWM, S3.IN1
  N3: Εξάρτημα1.D10_PWM/SS, S3.ENA
  N4: Εξάρτημα1.D11_PWM/MOSI, R3.Pin_0
  N5: Εξάρτημα1.D12/MISO, MS3.NC
  N6: Εξάρτημα1.D13/SCK, MS2.NC
  GND: Εξάρτημα1.GND, R1.Pin_0, S3.GND, VCC1.-, MS2.COM, MS3.COM, R2.Pin_0
  N7: Εξάρτημα1.D2, R1.Pin_1, S4.Pin_1, S4.Pin_2
  N8: Εξάρτημα1.D3_PWM, R2.Pin_1, S6.Pin_1, S6.Pin_2
  N9: Εξάρτημα1.D4, BREAKOUT1.In_1
  N10: Εξάρτημα1.D5_PWM, BREAKOUT1.In_2
  N11: Εξάρτημα1.D6_PWM, BREAKOUT1.In_3
  N12: Εξάρτημα1.D7, BREAKOUT1.In_4
  N13: Εξάρτημα1.5V, S4.Pin_3, S4.Pin_4, S6.Pin_3, S6.Pin_4
  N14: S3.12V, VCC1.+
  N15: S3.M1-01, M1.pin_2
  N16: S3.M1-02, M1.pin_1
  N17: BREAKOUT1.RED_wire, MOTOR1.RED
  N18: BREAKOUT1.ORANGE_wire, MOTOR1.ORANGE
  N19: BREAKOUT1.YELLOW_wire, MOTOR1.YELLOW
  N20: BREAKOUT1.PINK_wire, MOTOR1.PINK
  N21: BREAKOUT1.BLUE_wire, MOTOR1.BLUE
  N22: ΕΠΑΓΩΓΙΚΟΣ_ΑΙΣΘΗΤΗΡΑΣ.pin1, R3.Pin_1
  N23: ΕΠΑΓΩΓΙΚΟΣ_ΑΙΣΘΗΤΗΡΑΣ.pin2, 12V_Τροφοδοτικό.GND
  N24: ΕΠΑΓΩΓΙΚΟΣ_ΑΙΣΘΗΤΗΡΑΣ.pin3, 12V_Τροφοδοτικό.VCC

notes:
  Επαγωγικός αισθητήρας:
  Καφέ: 12V
  Μπλε: Γείωση
  Μαύρο: σήμα
  ΠΡΟΣΟΧΗ:
  Στην είσοδο 11 που έρχεται το σήμα του αισθητήρα
  να ενεργοποιηθεί η pullup αντίσταση.
  Ο ένας μικροδιακόπτης μπαίνει στη μία άκρη και ο άλλος στην άλλη, έτσι ώστε να ενεργοποιούνται από το φορείο.
  Αυτό είναι το μοτέρ του εκτυπωτή (που κινεί το φορείο).
  Αυτό το stepper motor βρίσκεται πάνω στο φορείο και ανατρέπει τον κάδο προς τα δεξιά ή προς τα αριστερά.
  ΠΡΟΣΟΧΗ:
  Ενεργοποιούμε τις εσωτερικές pullup αντιστάσεις των pin 12 και pin 13.

custom parts:
  H-Bridge with L298N: h-bridge
  ULN2003A breakout board: ULN2003A 7-way Darlington Transistor Driver on breakoutboard
  BGL-My Micro Switch: Μικροδιακόπτης με μεγάλη λαβή.
