# Fritzing sketch IoT-Full (saved by Fritzing 0.9.3b)
breadboards: 1

parts:
  Εξάρτημα1 = Arduino Uno (Rev3)
  U2 = ESP8266 WiFi Module [part_number=ESP8266]
  R1 = Resistor [tolerance=±5% resistance=1k package=THT]
  R2 = Resistor [tolerance=±5% resistance=2.2k package=THT]
  R3 = Resistor [tolerance=±5% resistance=10k package=THT]
  R4 = Resistor [tolerance=±5% resistance=10k package=THT]
  Εξωτερική_τροφοδοσία = Power plug [part_number=5V-15V]
  LD1117 = V_REG_LD1117VXX [package=78xxl]
  C2 = Electrolytic Capacitor [capacitance=100µF package="100 mil [THT, electrolytic]"]
  C3 = Ceramic Capacitor [capacitance=0.1µF package="100 mil [THT, multilayer]"]
  SparkFun_CSS811 = SparkFun_CSS811_Breakout [part_number=14193]
  LCD1 = LCD screen
  R5 = Trimmer Potentiometer [maximum_resistance=10kΩ package=THT]
  R6 = Resistor [tolerance=±5% resistance=220 package=THT]
  DHT11 = DHT11 Humitidy and Temperature Sensor
  U3 = L9110 H-bridge module [part_number="L9110 H-bridge"]
  Ανεμιστήρας_Οροφής = DC Motor

nets:
  N1: Εξάρτημα1.A4/SDA, SparkFun_CSS811.SDA
  N2: Εξάρτημα1.A5/SCL, SparkFun_CSS811.SCL
  N3: Εξάρτημα1.D8, U3.A-IB
  N4: Εξάρτημα1.D9_PWM, U3.A-IA
  N5: Εξάρτημα1.D11_PWM/MOSI, LCD1.E
  N6: Εξάρτημα1.D12/MISO, LCD1.RS
  N7: Εξάρτημα1.D13/SCK, DHT11.DATA
  GND: Εξάρτημα1.GND, U2.GPIO_2, U2.GND, R2.Pin_0, Εξωτερική_τροφοδοσία.GND, LD1117.GND, C2.-, C3.1, SparkFun_CSS811.GND, LCD1.VSS, LCD1.R/W, LCD1.LED-, R5.leg1, DHT11.GND, U3.GND
  N8: Εξάρτημα1.D2, LCD1.DB7
  N9: Εξάρτημα1.D3_PWM, LCD1.DB6
  N10: Εξάρτημα1.D4, LCD1.DB5
  N11: Εξάρτημα1.D5_PWM, LCD1.DB4
  N12: Εξάρτημα1.D6_PWM, U2.TXD
  N13: Εξάρτημα1.D7, R1.Pin_1
  VDD: Εξάρτημα1.5V, LCD1.VDD, R5.leg2, R6.Pin_0, DHT11.VDD, U3.VCC
  N14: U2.RXD, R1.Pin_0, R2.Pin_1
  VCC: U2.VCC, R3.Pin_0, R4.Pin_0, LD1117.OUT, C3.0, SparkFun_CSS811.3.3V
  N15: U2.GPIO_0, U2.RST, R3.Pin_1
  N16: U2.CH_PD, R4.Pin_1
  N17: Εξωτερική_τροφοδοσία.VCC, LD1117.IN, C2.+
  N18: LCD1.V0, R5.wiper
  N19: LCD1.LED+, R6.Pin_1
  N20: U3.MOTOR_A-A, Ανεμιστήρας_Οροφής.pin_2
  N21: U3.MOTOR_A-B, Ανεμιστήρας_Οροφής.pin_1

notes:
  UNO <=> ESP8266
  7 (softwareTX) => RX (κίτρινο)
  6 (softwareRX) <= TX (πράσινο)
  Για το RX του ESP απαιτείται διαιρέτης τάσης(2.2ΚΩ-1ΚΩ), διότι οι είσοδοι του ESP είναι 3.3V, ενώ η έξοδος του arduino είναι 5V.
  ESP8266
  Vcc => 3.3V
  GND => GND
  RST => 3.3V (μέσω 10ΚΩ)
  CH_PD => 3.3V (μέσω 10ΚΩ)
  Ο ρυθμιστής τάσης LD1117 τροφοδοτεί με 3.3V το ESP8266 και το CSS811.

custom parts:
  ESP8266 WiFi Module: Generic WiFi Module based on the ESP8266 with onboard PCB antenna and UART communications
  SparkFun_CSS811_Breakout: The CCS811 Air Quality Breakout is a digital gas sensor solution that senses a wide range of Total Volatile Organic Compounds (TVOCs), including equivalent carbon dioxide (eCO2) and metal oxide (MOX) levels. VOCs are often categorized as pollutants and/or sensory irritants and can come from a variety of sources like construction materials (paint, carpet, etc.), machines (copiers, processors,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
  DHT11 Humitidy and Temperature Sensor: DHT11 Humidity and Temperature Sensor
